# Fritzing sketch alarm_schema-20171231-no-relay (saved by Fritzing 0.9.3b)
breadboards: 1

parts:
  Součástka2 = Logic Level Converter
  LED2 = LED - 5mm [color="Green (570nm)" package="5 mm [THT]"]
  Součástka3 = Breadboard Power Supply Board SMD
  Espessif_Serial_Wifi_Modul_1 = ESP8266 ESP01 [part_number=ESP8266 package=THT]
  R3 = Resistor [tolerance=±5% resistance=4.7k package=THT]
  PIR1 = PIR sensor
  Součástka4 = Arduino Nano (Rev3.0)
  R1 = Resistor [tolerance=±5% resistance=10k package="0805 [SMD]"]
  C2 = Electrolytic Capacitor [capacitance=1µF voltage=16V package="1010 [SMD, electrolytic]"]
  KEYPAD1 = Membrane Matrix Keypad
  LED3 = smd LED [color="Red (633nm)" package="1206 [SMD]"]
  R4 = Resistor [tolerance=±5% resistance=10k package="0805 [SMD]"]

nets:
  N1: Součástka2.TX2_LV, Espessif_Serial_Wifi_Modul_1.RXD
  N2: Součástka2.RX2_LV, Espessif_Serial_Wifi_Modul_1.TXD
  GND: Součástka2.GND, Součástka3.GND, Espessif_Serial_Wifi_Modul_1.GND, PIR1.GND, Součástka4.GND, R1.Pin_0, C2.-, R4.Pin_0
  VCC: Součástka2.LV, Součástka3.VCC, Espessif_Serial_Wifi_Modul_1.VCC, R3.Pin_1, C2.+
  VDD: Součástka2.HV, PIR1.VDD, Součástka4.VIN
  N3: Součástka2.RX2_HV, Součástka4.D10
  N4: Součástka2.TX2_HV, Součástka4.D12/MISO
  N5: LED2.cathode, R1.Pin_1
  N6: LED2.anode, Součástka4.A3
  N7: Espessif_Serial_Wifi_Modul_1.CH_PD, R3.Pin_0
  N8: PIR1.SIG, Součástka4.D9
  N9: Součástka4.D2, KEYPAD1.7
  N10: Součástka4.D3, KEYPAD1.6
  N11: Součástka4.D4, KEYPAD1.5
  N12: Součástka4.D5, KEYPAD1.4
  N13: Součástka4.D6, KEYPAD1.3
  N14: Součástka4.D7, KEYPAD1.2
  N15: Součástka4.D8, KEYPAD1.1
  N16: Součástka4.A2, LED3.anode
  N17: LED3.cathode, R4.Pin_1

custom parts:
  ESP8266 ESP01: Generic WiFi Module based on the ESP8266 with onboard PCB antenna and UART communications
  Membrane Matrix Keypad: Membrane Matrix 3x4 Keypad
