# Fritzing sketch alarm_schema (saved by Fritzing 0.9.3b)
breadboards: 1

parts:
  Součástka2 = Logic Level Converter
  LED2 = LED - 5mm [color="Green (570nm)" package="5 mm [THT]"]
  Součástka3 = Breadboard Power Supply Board SMD
  Espessif_Serial_Wifi_Modul_1 = ESP8266 ESP01 [part_number=ESP8266 package=THT]
  R3 = Resistor [tolerance=±5% resistance=4.7k package=THT]
  PIR1 = PIR sensor
  Součástka4 = Arduino Nano (Rev3.0)
  R1 = Resistor [tolerance=±5% resistance=10k package="0805 [SMD]"]
  C2 = Electrolytic Capacitor [capacitance=1µF voltage=16V package="1010 [SMD, electrolytic]"]
  KEYPAD1 = Membrane Matrix Keypad
  LED3 = smd LED [color="Red (633nm)" package="1206 [SMD]"]
  R4 = Resistor [tolerance=±5% resistance=10k package="0805 [SMD]"]
  KY-1 = Keyes Relay [package=THT]

nets:
  N1: Součástka2.TX2_LV, Espessif_Serial_Wifi_Modul_1.RXD
  N2: Součástka2.RX2_LV, Espessif_Serial_Wifi_Modul_1.TXD
  GND: Součástka2.GND, Součástka3.GND, Espessif_Serial_Wifi_Modul_1.GND, PIR1.GND, Součástka4.GND, R1.Pin_0, C2.-, R4.Pin_0, KY-1.ground
  N3: Součástka2.LV, Espessif_Serial_Wifi_Modul_1.VCC, R3.Pin_1, C2.+, KY-1.NO
  VDD: Součástka2.HV, PIR1.VDD, Součástka4.VIN, KY-1.power
  N4: Součástka2.RX2_HV, Součástka4.D10
  N5: Součástka2.TX2_HV, Součástka4.D12/MISO
  N6: LED2.cathode, R1.Pin_1
  N7: LED2.anode, Součástka4.A3
  N8: Součástka3.VCC, KY-1.C
  N9: Espessif_Serial_Wifi_Modul_1.CH_PD, R3.Pin_0
  N10: PIR1.SIG, Součástka4.D9
  N11: Součástka4.D2, KEYPAD1.7
  N12: Součástka4.D3, KEYPAD1.6
  N13: Součástka4.D4, KEYPAD1.5
  N14: Součástka4.D5, KEYPAD1.4
  N15: Součástka4.D6, KEYPAD1.3
  N16: Součástka4.D7, KEYPAD1.2
  N17: Součástka4.D8, KEYPAD1.1
  N18: Součástka4.D11/MOSI, KY-1.signal
  N19: Součástka4.A2, LED3.anode
  N20: LED3.cathode, R4.Pin_1

notes:
  Since the ESP8266 01 module is not stable and time to time it stops responding, it is possible to restart esp8266 programatically via the added relay. Simply, when the arduino does not receive the right response, the pin 11 is set to HIGH for several seconds which causes that the ESP8266 is switched off for that period. After ends of period the esp8266 is switched on automatically again.

custom parts:
  ESP8266 ESP01: Generic WiFi Module based on the ESP8266 with onboard PCB antenna and UART communications
  Membrane Matrix Keypad: Membrane Matrix 3x4 Keypad
  Keyes Relay: The Keyes 5V relay module is suitable for SCM development, home appliance control. It uses a 5V~12V TIL control signal which can control DC / AC signal.
